# Fritzing sketch Fritzing-BinaryClock (saved by Fritzing 0.8.5b)
breadboards: 1

parts:
  U1 = atmega168 [package=dip]
  XTAL1 = Crystal [frequency="16 Mhz" package=SMD]  # not connected
  U3 = 74HC595 [part_number=Columns package="DIP16 [THT]"]
  U2 = 74HC595 [part_number=Rows package="DIP16 [THT]"]
  IC1 = ULN2803A [package=THT]

nets:
  VCC: U1.VCC, U3.MR, U3.VCC, U2.MR, U2.VCC
  GND: U1.GND, U3.GND, U3.OE, U2.GND, U2.OE, IC1.0V
  N1: U1.D8, U3.ST_CP, U2.ST_CP
  N2: U1.D11_(PWM), U3.DS
  N3: U1.D12, U3.SH_CP, U2.SH_CP
  N4: U3.Q1, IC1.In_2
  N5: U3.Q2, IC1.In_3
  N6: U3.Q3, IC1.In_4
  N7: U3.Q4, IC1.In_5
  N8: U3.Q5, IC1.In_6
  N9: U3.Q6, IC1.In_7
  N10: U3.Q7, IC1.In_8
  N11: U3.Q7', U2.DS
  N12: U3.Q0, IC1.In_1
